# Fritzing sketch lcd_thermometer (saved by Fritzing 0.8.7b)
circuit board: 8.6cm x 5.7cm
breadboards: 1

parts:
  U2 = Voltage Regulator - 5V [package="TO220 [THT]"]
  C5 = Electrolytic Capacitor [capacitance=1µF voltage=35V package="100 mil [THT, electrolytic]"]
  C6 = Electrolytic Capacitor [capacitance=10µF voltage=10V package="100 mil [THT, electrolytic]"]
  C9 = Ceramic Capacitor [capacitance=100nF voltage=10V package="200 mil [THT, multilayer]"]
  LED1 = LED - 5mm [color="Blue (470nm)" package="5 mm [THT]"]
  SW1 = Rotary Encoder [part_number=318-ENC130175F-12PS package=encoder]
  S2 = Momentary Switch [package=ksa_sealed_tac_switch]
  U3 = atmega328p [package=dip]
  XTAL1 = Crystal [frequency="16 Mhz" package=THT]
  T1 = Square Sealed Panel Control [part_number=3310P-001-103L package="TO92 [THT]"]
  J2 = screw terminal, 3 pins
  R10 = Resistor [tolerance=±5% resistance=4.7k package=THT]
  R9 = Resistor [tolerance=±5% resistance=4.7k package=THT]
  C8 = Ceramic Capacitor [capacitance=10nF voltage=10V package="100 mil [THT, multilayer]"]
  J1 = screw terminal, 3 pins
  LCD2 = Basic 16x2 Character LCD Yellow on Blue
  J5 = male pin header, 3 pins [form="♂ (male)"]
  D1 = Schottky Diode [part_number=1N5817 package="300 mil [THT]"]
  J7 = AVR ISP 6 Pin [package=2x3]  # not connected
  J8 = AVR ISP 6 Pin [package=2x3]  # not connected
  J9 = AVR ISP 6 Pin [package=2x3]  # not connected
  J10 = AVR ISP 6 Pin [package=2x3]  # not connected
  J11 = AVR ISP 6 Pin [package=2x3]  # not connected
  J12 = AVR ISP 6 Pin [package=2x3]
  J13 = AVR ISP 6 Pin [package=2x3]  # not connected
  J6 = AVR ISP 6 Pin [package=2x3]
  R8 = Resistor [tolerance=±5% resistance=10k package=THT]
  R7 = Resistor [tolerance=±5% resistance=220 package=THT]
  J14 = male pin header, 2 pins [form="♂ (male)"]
  J15 = male pin header, 2 pins [form="♂ (male)"]
  U4 = Programmable Precision Reference [part_number=TL431 package="TO92 [THT]"]
  C10 = Ceramic Capacitor [capacitance=1µF package="100 mil [THT, multilayer]"]
  R13 = Resistor [tolerance=±0.1% resistance=560 package="0603 [SMD]"]
  R14 = Resistor [tolerance=±0.1% resistance=8.2k package="0603 [SMD]"]
  R15 = Resistor [tolerance=±0.1% resistance=560 package="0603 [SMD]"]
  R16 = Resistor [tolerance=±0.1% resistance=15k package="0603 [SMD]"]
  R17 = Resistor [tolerance=±0.1% resistance=15k package="0603 [SMD]"]
  R18 = Resistor [tolerance=±0.1% resistance=15k package="0603 [SMD]"]
  J18 = male pin header, 1 pin [form="♂ (male)"]
  J17 = male pin header, 1 pin [form="♂ (male)"]
  J16 = male pin header, 1 pin [form="♂ (male)"]
  J19 = male pin header, 1 pin [form="♂ (male)"]
  C4 = Ceramic Capacitor [capacitance=10pF package="100 mil [THT, multilayer]"]
  C3 = Ceramic Capacitor [capacitance=10pF package="100 mil [THT, multilayer]"]

nets (from the pcb view):
  N1: U2.input_voltage, C5.+, D1.cathode, C10.0, R13.Pin_0
  N2: U2.GND, J19.pin1
  N3: U2.output_voltage, C6.+, U3.VCC, U3.AVCC, J12.1, J6.2, R8.Pin_0
  N4: C9.0, S2.3, S2.4, U3.RESET, R8.Pin_1
  N5: C9.1, J5.pin1
  N6: LED1.cathode, R7.Pin_0
  N7: LED1.anode, U3.D13
  N8: SW1.X, U3.D4
  N9: SW1.A, U3.D3_(PWM)
  N10: SW1.B, U3.D2
  N11: U3.D0_(RX), J5.pin2
  N12: U3.D1_(TX), J5.pin3
  N13: U3.GND#7, J16.pin1
  N14: U3.XLAT1, XTAL1.pin_1, C4.0
  N15: U3.XLAT2, XTAL1.pin_0, C3.0
  N16: U3.D5_(PWM), LCD2.DB4
  N17: U3.D6_(PWM), LCD2.DB5
  N18: U3.D7, LCD2.DB6
  N19: U3.D8, LCD2.DB7
  N20: U3.D9_(PWM), LCD2.LED+
  N21: U3.D10_(PWM), R9.Pin_0, J1.pin2
  N22: U3.D11_(PWM), J2.pin2, R10.Pin_0
  N23: U3.D12, U4.A, R16.Pin_1, R18.Pin_1
  N24: U3.AREF, U4.K, R13.Pin_1, R14.Pin_0
  N25: U3.GND#21, J18.pin1
  N26: U3.A0, T1.CW, J2.pin3, R10.Pin_1, R9.Pin_1, C8.1, J1.pin3, LCD2.VDD
  N27: U3.A1, LCD2.RS
  N28: U3.A2, LCD2.E
  N29: U3.A3, R17.Pin_0, R18.Pin_0
  N30: T1.Wiper, LCD2.V0
  N31: D1.anode, J15.pin1, J15.pin2, R17.Pin_1
  N32: J12.2, J6.1, J17.pin1
  N33: J14.pin1, J14.pin2
  N34: U4.R, R14.Pin_1, R15.Pin_0, R15.Pin_1, R16.Pin_0
  N35: C4.1, C3.1

notes:
  Contrast Adjust
  +
  -
  Copyright
  2014
  Chris
  Evich
  rev. 2
  lcd_thermometer, Copyright 2014 Chris Evich, 2

custom parts:
  Rotary Encoder: This is a 12-step rotary encoder with a nice ‘clicking’ feel. It’s breadboard friendly, and has a pretty handy select switch (by pushing in on the knob). The encoder is different from a potentiometer in that an encoder has full rotation without limits. The unit outputs gray code so that you can tell how much and in which direction the encoder has been turned.
  atmega328p: Atmel ATmega328 microcontroller. The hardware hacker favorite.
  Square Sealed Panel Control: * Conductive plastic * PC board and bushing mount * Plastic or metal bushing and plastic shaft * Withstands typical industrial washing processes * Compact package saves board and panel space
  Basic 16x2 Character LCD Yellow on Blue: This is a basic 16 character by 2 line display with a Blue background and a Yellow backlight. Utilizes the extremely common HD44780 parallel interface chipset (datasheet). Interface code is freely available. You will need ~11 general I/O pins to interface to this LCD screen. Includes yellow LED backlight. These modules are the thin type.
  Programmable Precision Reference: Three-terminal programmable precision voltage reference.

// code stored in the sketch: lcd_thermometer.h
#ifndef LCD_THERMOMETER_H
#define LCD_THERMOMETER_H

/*
 * Macros
 */

//#define NODEBUG
#ifndef NODEBUG
    #define DEBUG
#endif

#ifdef DEBUG
    #define D(...) Serial.print(__VA_ARGS__)
    #define DL(...) Serial.println(__VA_ARGS__)
#else
    #define D(...) if (false)
    #define DL(...) if (false)
#endif // DEBUG

struct Data {
    // types

     static const struct DispState {
        static const uint8_t now = 0;
        static const uint8_t one = 1;
        static const uint8_t four = 2;
        static const uint8_t snooze = 3;
    } DispState;

     static const struct TransState {
        static const uint8_t enter = 0;
        static const uint8_t hold = 1;
        static const uint8_t exit = 2;
    } TransState;

     static const struct LcdBlState {
        static const uint8_t up = 0;
        static const uint8_t down = 2;
        static const uint8_t equal = 3;
        static const uint8_t on = 4;
        static const uint8_t off = 5;
    } LcdBlState;

    // Peripheral Power
    static const uint8_t PIN_PERIPH_POWER = 11;

    // LCD Interface
    static const uint8_t PIN_LCD_RS = A0;
    static const uint8_t PIN_LCD_EN = A1;
    static const uint8_t PIN_LCD_DA0 = A2;
    static const uint8_t PIN_LCD_DA1 = A3;
    static const uint8_t PIN_LCD_DA2 = 4;
    static const uint8_t PIN_LCD_DA3 = 5; // funky pwm
    static const uint8_t PIN_LCD_DA4 = 6; // funky pwm
    static const uint8_t PIN_LCD_DA5 = 7;
    static const uint8_t PIN_LCD_DA6 = 8;
    static const uint8_t PIN_LCD_DA7 = 12;
    static const uint8_t PIN_LCD_BL = 3; // pwm

    // LCD Details
    static const uint8_t LCD_COLS = 20;
    static const uint8_t LCD_ROWS = 2;

    // One Wire Bus
    static const uint8_t PIN_OWB_LOCAL = 9; // i2c SDA
    static const uint8_t PIN_OWB_REMOTE = 10; // i2c SCL
    static const uint8_t MAXRES = 10;
    static const int16_t FAULTTEMP = 12345;

    // Doing "work" indicator
    static const uint8_t PIN_STATUS_LED = 13;

    // Timing data
    static const uint16_t SLEEP_MSEC        = 8000; // 8 seconds
    static const uint8_t SLEEP_CYCLES       = 75; // 10 minutes
    static const Millis LCD_UPDATE_INTERVAL = 1000; // < 1000ms is unreadable
    static const Millis TEMP_SAMPLE_INTVL   = 600000; // 10 minutes (in ms)
    static const Millis TEMP_SMA_WINDOW_S   = 3600000; // 1 hour SMA (short)
    static const Millis TEMP_SMA_WINDOW_L   = 14400000; // 4 hour SMA (long)
                                      // (TEMP_SMA_WINDOW_S / TEMP_SAMPLE_INTVL);
    static const uint16_t SMA_POINTS_S = 6;
                                      // (TEMP_SMA_WINDOW_L / TEMP_SAMPLE_INTVL);
    static const uint16_t SMA_POINTS_L = 24;
    // Allow re-use of lcdBlStateTimer for transState
    static const uint8_t LCD_BL_RAMP_DIVISIONS = 20;  // updates per second
                                     // 1000 / LCD_BL_RAMP_DIVISIONS;
    const Millis LCD_BL_RAMP_INTERVAL = 50;  // ms intvl btwn ticks
    // Durations, in ramp-div updates (ticks) for each stage
    static const uint16_t LCD_BL_RAMP_TICKS = 20;  // 1-second in ticks
    static const uint16_t LCD_BL_EQ_TICKS = 10; //  .5-seconds in ticks
    static const uint16_t LCD_BL_ON_TICKS = 160;  // 8-seconds in ticks
    static const uint16_t LCD_BL_OFF_TICKS = 0;  // zero-time

    // max value for dispCycles
    static const uint8_t MAX_DISPLAY_CYCLES = 3;  // now, one, four...before snooze
    // Temperature unit
    static const bool CELSIUS = false;
    static const char DEGREE_CHAR = 223;

    // OneWire bus and sensors
    OneWire owb_local;
    OneWire owb_remote;
    MaxDS18B20::MaxRom rom_local;
    MaxDS18B20::MaxRom rom_remote;
    MaxDS18B20* max_local_p;
    MaxDS18B20* max_remote_p;

    // lcd double-buffer
    LCD lcd;
    uint8_t lcdBlVal;  // PWM value to set (0-255)

    // master clock
    Millis current_time;
    volatile uint8_t sleepCycleCounter;
    unsigned long sleepAdvance; // timer does not count during sleep

    // Temperature readings
    int16_t now_local;
    int16_t now_remote;
    SimpleMovingAvg sma_local_s;
    SimpleMovingAvg sma_local_l;
    SimpleMovingAvg sma_remote_s;
    SimpleMovingAvg sma_remote_l;

    // serviced by main loop, transitions in transState
    StateMachine dispState;  // data display state (now, 1h, 4h,, snooze)
    uint8_t dispCycles;  // number of times through dispState

    // serviced by dispState, transitions in lcdBlState
    StateMachine transState;  // inner-display state (enter, hold, exit, next)
    uint8_t lcdblStateCache;  // Cache during dispState cycle

    // serviced by transState, transitions in lcdBLStateTimer
    StateMachine lcdBlState;    // backlight state (ramp up, ramp-down, hold-on, hold-off)

    // inc dispTics every LCD_BL_RAMP_INTERVAL miliseconds
    TimedEvent lcdBlStateTimer; // transition timer for lcdBlState
    uint16_t lcdblTicks;  // nr lcdBlStateTimer fires


    // Member Functions
    // Constructor
    Data(void);
    void setup(void);
    void loop(void);
    void init_max(OneWire& owb, MaxDS18B20::MaxRom& rom, MaxDS18B20*& max_pr) const;
    void start_conversion(MaxDS18B20::MaxRom& rom, MaxDS18B20*& max_pr) const ;
    void wait_conversion(MaxDS18B20::MaxRom& rom, MaxDS18B20*& max_pr)const ;
    int16_t get_temp(MaxDS18B20::MaxRom& rom, MaxDS18B20*& max_pr)const ;
    int16_t sma_append(SimpleMovingAvg& sma, uint16_t temp);
} data;

#endif // LCD_THERMOMETER_H

// code stored in the sketch: lcd_thermometer.ino
/**********************************************************************
 Notes:

LCD:

    12345678901234567890
    Now  Lcl Rmt   Diff
    000.0    000.0 000.0

    1hA  Lcl Rmt   Diff
    000.0    000.0 000.0

    4hA  Lcl Rmt   Diff
    000.0    000.0 000.0

    * backlight:
        * "Up" blink if current temp > 1-hour temp
              ****     ****     ****
             *****    *****    *****
            ******   ******   ******
           *******  *******  *******
           |--|--|  repeat once per categoty
            1s 8s

        * "Down" blink if current temp < 1-hour temp
          ****     ****     ****
          *****    *****    *****
          ******   ******   ******
          *******  *******  *******
           |--|--|  repeat once per categoty
            1s 8s

Non-display:
    * Sleep for 8s (8000ms)
    * measure temp for 1s (1000ms)
    * misc. calc for 1s   (1000ms)

Data:
0) measure temp every 10 minutes -> (1 A + 1 B = 2)
1) every 10 minutes, save temp -> 1-hour SMA (6 A + 6 B readings = 12)
2) every hour, also save temp -> 24-hour SMA (24A + 24B = 48)

Memory requirements for data:
* class SimpleMovingAvg: 8 bytes + 2 * max_points bytes
* "live" A & B readings @ 2-bytes == 4 bytes total
* 60mSMA A & B @ 20-bytes        == 40 bytes total
* 24hSMA A & B @ 56-bytes       == 112 bytes total
                               --------------------
                                   156 bytes

Power:

35-45 mA ~= 40 hours w/ AA source
   10 mA ~= 175 hours w/ AA source

----------------------------------------------------

Measuring 4xAA battery:

z1 = 400k ohm
z2 = 1m ohm

>>> def vdiv(vin, z1, z2):
...     return vin * (z2 / (z1 + z2))

Max ~= 7.0 volts

>>> print vdiv(7.0, 400000.0, 1000000.0)
5.0

>>> print vdiv(4.5, 400000.0, 1000000.0)
3.21428571429

setup() {
    connect vout to analog pin
    connect z2 through OUTPUT gpio pin }
    set gpio HIGH (source)

check_battery() {
    set gpio LOW (sink)
    read analog pin
    set gpio HIGH (source)
    # map read value (0 and 1023)
    volts = map(red, 0, 1023, 5000, 0)
    battery full = 5000
    battery empty = 3214
    battert percent = map(volts, 3214, 5000, 0, 100)
    return battert percent
}
**********************************************************************/
#include <avr/sleep.h>
#include <avr/power.h>
#include <avr/wdt.h>
#include <stdlib.h>
#include <LiquidCrystal.h>
#include <OneWire.h>
#include "MaxDS18B20.h"
#include "MovingAvg.h"
#include "TimedEvent.h"
#include "StateMachine.h"
#include "lcd.h"
#include "lcd_thermometer.h"

/*
 *  Public Member Functions
 */

Data::Data(void)
           :
           owb_local(PIN_OWB_LOCAL),
           owb_remote(PIN_OWB_REMOTE),
           now_local(FAULTTEMP),
           now_remote(FAULTTEMP),
           sma_local_s(SMA_POINTS_S),
           sma_local_l(SMA_POINTS_L),
           sma_remote_s(SMA_POINTS_S),
           sma_remote_l(SMA_POINTS_L),
           lcd(PIN_LCD_RS, PIN_LCD_EN,
               PIN_LCD_DA0, PIN_LCD_DA1,
               PIN_LCD_DA2, PIN_LCD_DA3,
               PIN_LCD_DA4, PIN_LCD_DA5,
               PIN_LCD_DA6, PIN_LCD_DA7),
           dispState(sizeof(DispState) / sizeof(uint8_t),
                     DispState.now),
           transState(sizeof(TransState) / sizeof(uint8_t),
                      TransState.enter),
           lcdBlState(sizeof(LcdBlState) / sizeof(uint8_t),
                      LcdBlState.equal),
           lcdBlStateTimer(current_time, LCD_BL_RAMP_INTERVAL, lcdbl_event_equal_f),
           lcdblStateCache(LcdBlState.equal),
           lcdblTicks(0),
           dispCycles(0),
           sleepCycleCounter(0),
           sleepAdvance(0),
           lcdBlVal(255) { // no flicker @ start
    #ifdef DEBUG
    Serial.begin(115200);
    #endif // DEBUG
    DL(F("Initializing..."));

    D(F("Short SMA points: ")); D(SMA_POINTS_S);
    D(F(" Short SMA update interval (ms): ")); DL(TEMP_SAMPLE_INTVL);

    D(F("Long SMA points: ")); D(SMA_POINTS_L);
    D(F(" Long SMA update interval (ms): ")); DL(TEMP_SAMPLE_INTVL);

    D(F("LCD up/dn Ramp intvl (ms): ")); D(LCD_BL_RAMP_INTERVAL);
    D(F("LCD ramp ticks (1-second divisions): ")); DL(LCD_BL_RAMP_TICKS);

    D(F("LCD equal ticks: ")); D(LCD_BL_EQ_TICKS);
    D(F(" LCD on ticks: ")); DL(LCD_BL_ON_TICKS);

    DL(F("Setting up WDT sleep mode..."));
    /* Clear the reset flag. */
    MCUSR &= ~(1<<WDRF);
    /* In order to change WDE or the prescaler, we need to
     * set WDCE (This will allow updates for 4 clock cycles).
     */
    WDTCSR |= (1<<WDCE) | (1<<WDE);
    /* set new watchdog timeout prescaler value */
    WDTCSR = 1<<WDP0 | 1<<WDP3; /* 8.0 seconds */
    /* Enable the WD interrupt (note no reset). */
    WDTCSR |= _BV(WDIE);
    // Maximum power savings
    set_sleep_mode(SLEEP_MODE_PWR_DOWN);

    D(F("Setup LCD pins:"));
    D(F(" RS- ")); D(PIN_LCD_RS);
    pinMode(PIN_LCD_RS, OUTPUT);
    D(F(" EN- ")); D(PIN_LCD_EN);
    pinMode(PIN_LCD_EN, OUTPUT);
    D(F(" D0- ")); D(PIN_LCD_DA0);
    pinMode(PIN_LCD_DA0, OUTPUT);
    D(F(" D1- ")); D(PIN_LCD_DA1);
    pinMode(PIN_LCD_DA1, OUTPUT);
    D(F(" D2- ")); D(PIN_LCD_DA2);
    pinMode(PIN_LCD_DA2, OUTPUT);
    D(F(" D3- ")); D(PIN_LCD_DA3);
    pinMode(PIN_LCD_DA3, OUTPUT);
    D(F(" D4- ")); D(PIN_LCD_DA4);
    pinMode(PIN_LCD_DA4, OUTPUT);
    D(F(" D5- ")); D(PIN_LCD_DA5);
    pinMode(PIN_LCD_DA5, OUTPUT);
    D(F(" D6- ")); D(PIN_LCD_DA6);
    pinMode(PIN_LCD_DA6, OUTPUT);
    D(F(" D7- ")); DL(PIN_LCD_DA7);
    pinMode(PIN_LCD_DA7, OUTPUT);

    D(F("Setting LCD Backlight pin (PWM) to output: ")); DL(PIN_LCD_BL);
    pinMode(PIN_LCD_BL, OUTPUT);

    D(F("Setting status LED pin to output: ")); DL(PIN_STATUS_LED);
    pinMode(PIN_STATUS_LED, OUTPUT);

    D(F("Setting OneWire power to output: ")); DL(PIN_OWB_POWER);
    pinMode(PIN_PERIPH_POWER, OUTPUT);
    digitalWrite(PIN_PERIPH_POWER, HIGH);

    D(F("Setting local OneWire bus pin to output: ")); DL(PIN_OWB_LOCAL);
    pinMode(PIN_OWB_LOCAL, OUTPUT);

    D(F("Setting remote OneWire bus pin to output: ")); DL(PIN_OWB_REMOTE);
    pinMode(PIN_OWB_REMOTE, OUTPUT);

    DL(F("Setting up sensor devices..."));
    init_max(owb_local, rom_local, max_local_p);
    init_max(owb_remote, rom_remote, max_remote_p);

    // setup time
    DL(F("Setting timer"));
    current_time = millis();
}

void Data::init_max(OneWire& owb,
                    MaxDS18B20::MaxRom& rom,
                    MaxDS18B20*& max_pr) const {
    while (true) {
        if (MaxDS18B20::getMaxROM(owb, rom, 0)) {
            if (max_pr == NULL)
                max_pr = new MaxDS18B20(owb, rom);
            max_pr->setResolution(MAXRES);
            if (!max_pr->writeMem())
                DL(F("Error: Device setup failed!"));
            else {
                D("Setup device: "); rom.serial_print();
                break;
            }
        }
        DL(F("Waiting for device presence..."));
        delay(1000);
    }
}

inline void Data::start_conversion(MaxDS18B20::MaxRom& rom,
                                   MaxDS18B20*& max_pr) const {
    D(F("Starting conversion on: ")); rom.serial_print();
    if (!max_pr->startConversion())
        DL(F("Error: Device disappeared!"));
}

inline void Data::wait_conversion(MaxDS18B20::MaxRom& rom,
                                  MaxDS18B20*& max_pr) const {
    D(F("Waiting for conversion on: ")); rom.serial_print();
    D(F("."));
    while (!max_pr->conversionDone()) {
        digitalWrite(PIN_STATUS_LED,
                     !digitalRead(PIN_STATUS_LED));
        D(F("."));
        delay(100);
    }
    DL(F("done"));
}

inline int16_t Data::get_temp(MaxDS18B20::MaxRom& rom,
                              MaxDS18B20*& max_pr) const {
    if (!max_pr->conversionDone())
        wait_conversion(rom, max_pr);
    digitalWrite(PIN_STATUS_LED, HIGH);
    D(F("Reading memory from device: ")); rom.serial_print();
    if (max_pr->readMem()) {
        if (data::CELSIUS) {
            D(F("Temperature: ")); D(max_pr->getTempC()); DL(F("°C"));
            digitalWrite(PIN_STATUS_LED, LOW);
            return max_pr->getTempC();
        } else {
            D(F("Temperature: ")); D(max_pr->getTempF()); DL(F("°F"));
            digitalWrite(PIN_STATUS_LED, LOW);
            return max_pr->getTempF();
        }
    }
    DL(F("Error reading memory!"));
    return FAULTTEMP;
}

inline int16_t Data::sma_append(SimpleMovingAvg& sma,
                                uint16_t temp) {
    if (temp != FAULTTEMP) {
        return sma.append(temp);
    } else {
        DL(F("Not recording faulty temperature!"));
        return FAULTTEMP;
    }
}


inline void Data::setup(void) {
    DL(F("Computing initial temperatures..."));
    start_conversion(data.rom_local, data.max_local_p);
    start_conversion(data.rom_remote, data.max_remote_p);

    // Conversion takes a while, do other stuff while it runs
    DL(F("Initializing LCD..."));
    lcd.begin(LCD_COLS, LCD_ROWS);

    DL(F("Setting up Data display state machine..."));
    dispState.define(DispState.now, now_f);
    dispState.define(DispState.one, one_f);
    dispState.define(DispState.four, four_f);
    dispState.define(DispState.snooze, snooze_f);

    D(F("Setting up transition state machine..."));
    transState.define(TransState.enter, enter_f);
    transState.define(TransState.hold, hold_f);
    transState.define(TransState.exit, exit_f);

    DL(F("Setting up backlight state machine..."));
    lcdBlState.define(LcdBlState.up, lcdbl_state_up_f);
    lcdBlState.define(LcdBlState.on, lcdbl_state_on_f);
    lcdBlState.define(LcdBlState.down, lcdbl_state_down_f);
    lcdBlState.define(LcdBlState.equal, lcdbl_state_equal_f);
    lcdBlState.define(LcdBlState.off, lcdbl_state_off_f);

    DL(F("Setting up local temp..."));
    now_local = get_temp(rom_local, max_local_p);
    sma_append(data.sma_local_s, now_local);
    sma_append(data.sma_local_l, now_local);

    DL(F("Setting up remote temp..."));
    now_remote = get_temp(rom_remote, max_remote_p);
    sma_append(data.sma_remote_s, now_remote);
    sma_append(data.sma_remote_l, now_remote);
}

inline void Data::loop(void) {
    current_time = millis() + (sleep_advance * 100);
    temp_update();  // now_local & now_remote
    short_smas.update();
    long_smas.update();
    current_time = millis() + (sleep_advance * 100);
    dispState.service(); // and all lower nested-states
}

/////////////////////// temp measurement

void temp_update(void) {
    if (data.max_local_p->conversionDone()) {
        D(F("Updating local reading..."));
        data.now_local = data.get_temp(data.rom_local, data.max_local_p);
        data.start_conversion(data.rom_local, data.max_local_p);
    }
    if (data.max_remote_p->conversionDone()) {
        D(F("Updating remote reading..."));
        data.now_remote = data.get_temp(data.rom_remote, data.max_remote_p);
        data.start_conversion(data.rom_remote, data.max_remote_p);
    }
}

/////////////////////// DispState servicers

void lcdbl_helper_init(uint8_t lcd_bl_state) {
    data.lcdblTicks = 0;
    switch (lcd_bl_state) {
        case Data::LcdBlState::up:
            DL(F("Initializing backlight up transition"));
            data.lcdBlStateTimer.reInitIfNot(lcdbl_event_up_f);
            data.lcdBlVal = 0;
            break;
        case Data::LcdBlState::equal:
            DL(F("Initializing backlight equal transition"));
            data.lcdBlStateTimer.reInitIfNot(lcdbl_event_equal_f);
            data.lcdBlVal = 255;
            break;
        case Data::LcdBlState::on:
            DL(F("Initializing backlight on transition"));
            data.lcdBlStateTimer.reInitIfNot(lcdbl_event_on_f);
            data.lcdBlVal = 255;
            break;
        case Data::LcdBlState::down:
            D(F("Backlight down ramp "));
            data.lcdBlStateTimer.reInitIfNot(lcdbl_event_down_f);
            data.lcdBlVal = 255;
        case Data::LcdBlState::off:
            DL(F("Initializing backlight off transition"));
            data.lcdBlStateTimer.reInitIfNot(lcdbl_event_off_f);
            data.lcdBlVal = 0;
    }
}

void choose_updown(void) {  // ONCE per display change
    uint16_t sma_value = data.sma_remote_s.value();

    if (data.now_remote > sma_value) {
        data.lcdBlState.setCurrentId(Data::LcdBlState::up);
    } else if (data.now_remote < sma_value) {
        data.lcdBlState.setCurrentId(Data::LcdBlState::down);
    } else {
        data.lcdBlState.setCurrentId(Data::LcdBlState::equal);
    }
    data.lcdblStateCache = data.lcdBlState.getCurrentId();
}

void disp_header(PGM_P header_p) {
    char c = pgm_read_byte(header_p);
    uint8_t offset = 0;
    for (; c != 0; c = pgm_read_byte(header_p++))
        data.lcd.lcdWork[offset++] = c;
}

void disp_temp(uint16_t temp, uint8_t offset) {
    const uint8_t ibuff_len = 6;
    char ibuff[ibuff_len] = {0};
    int16_t dig = temp / 100;
    uint16_t dec = temp % 100;

    // round up or down to nearest tenth
    if (dec < 6)
        dec = 0;
    else if ((dec > 5) and (dec < 10))
        dec = 1;
    else
        dec = dec / 10; // truncate hundreths

    itoa(dig, ibuff, 10);
    for (uint8_t i=0; i < strnlen(ibuff, ibuff_len); i++)
        data.lcd.lcdWork[offset + i] = ibuff[i];
    // only room for 3 digits + 1 decimal
    data.lcd.lcdWork[offset + 3] = '.';
    itoa(dec, ibuff, 10);
    data.lcd.lcdWork[offset + 4] = ibuff[0]; // guaranteed only tenths
}

void disp_unit(uint8_t offset) {
    data.lcd.lcdWork[offset] = Data::DEGREE_CHAR; // degree character
    if (data.CELSIUS)
        data.lcd.lcdWork[offset + 1] = 'c';
    else
        data.lcd.lcdWork[offset + 1] = 'f';
}

void now_f(StateMachine* state_machine) {
   /*              1111111111
    *    01234567890123456789
    *    Now  Lcl Rmt   Diff
    *    000.0 *c 000.0 000.0
    */
    // copy header
    disp_header(PSTR("Now  Lcl Rmt   Diff"));
    disp_temp(data.now_local, Data::LCD_COLS);
    disp_unit(26);
    disp_temp(data.now_remote, Data::LCD_COLS + 9);
    disp_temp(abs(data.now_local - data.now_remote), Data::LCD_COLS + 15);
    // service state
    data.transState.service();
}

void one_f(StateMachine* state_machine) {
   /*              1111111111
    *    01234567890123456789
    *    1hMA lcl Rmt   Diff
    *    000.0 *c 000.0 000.0
    */
    const int16_t sma_local = data.sma_remote_s.value();
    const int16_t sma_remote = data.sma_remote_s.value();
    disp_header(PSTR("1hMA Lcl Rmt   Diff"));
    disp_temp(sma_local, Data::LCD_COLS);
    disp_unit(26);
    disp_temp(sma_remote, Data::LCD_COLS + 9);
    disp_temp(abs(sma_local - sma_remote), Data::LCD_COLS + 15);
    // service state
    data.transState.service();
}

void four_f(StateMachine* state_machine) {
   /*              1111111111
    *    01234567890123456789
    *    4hMA lcl Rmt   Diff
    *    000.0 *c 000.0 000.0
    */
    const int16_t sma_local = data.sma_remote_l.value();
    const int16_t sma_remote = data.sma_remote_l.value();
    disp_header(PSTR("4hMA Lcl Rmt   Diff"));
    disp_temp(sma_local, Data::LCD_COLS);
    disp_unit(26);
    disp_temp(sma_remote, Data::LCD_COLS + 9);
    disp_temp(abs(sma_local - sma_remote), Data::LCD_COLS + 15);
    // service state
    data.transState.service();
}

void snooze_f(StateMachine* state_machine) {
    D(F("Snoozing..."));
    digitalWrite(PIN_STATUS_LED, LOW);
    analogWrite(data.PIN_LCD_BL, 0);
    digitalWrite(PIN_PERIPH_POWER, LOW);
    power_all_disable();
    Millis sleepduration = millis();
    for (sleepCycleCounter=0; sleepCycleCounter < Data::SLEEP_CYCLES;) {
        sleep_enable(); // ZZzzzzzzzz
        sleep_disable(); // Woke up
    }
    sleepduration = millis() - sleepduration;
    power_all_enable();
    digitalWrite(PIN_PERIPH_POWER, HIGH);

    // seconds to add to current_time
    data.start_conversion(data.rom_local, data.max_local_p);
    data.start_conversion(data.rom_remote, data.max_remote_p);
    data.lcd.begin(LCD_COLS, LCD_ROWS);  // power lost, must re-initialize (slow!)
    D(F("Sleep duration: ")); DL(sleepduration);
    DL(F("Gathering post-snooze temp. readings"));
    temp_update();  // and start next conversion
    choose_updown(); // set up data.lcdBlState
    data.transState.setCurrentId(Data::TransState::enter);
    // Batteries will die before this overflows
    data.sleep_advance += (sleepduration / 100);
    data.dispState.setCurrentId(Data::DispState::now);
    data.dispCycles = 0;
    // enter always only handles up or equal
    if ((data.lcdblStateCache != Data::LcdBlState::up) ||
        (data.lcdblStateCache != Data::LcdBlState::equal))
        lcdbl_helper_init(Data::LcdBlState::off);
    else
        lcdbl_helper_init(data.lcdblStateCache); // up or equal
    DL(F("Updating local short SMA..."));
    data.sma_append(data.sma_local_s, data.now_local);
    DL(F("Updating remote short SMA..."));
    data.sma_append(data.sma_remote_s, data.now_remote);
    DL(F("Updating local long SMA..."));
    data.sma_append(data.sma_local_l, data.now_local);
    DL(F("Updating remote long SMA..."));
    data.sma_append(data.sma_remote_l, data.now_remote);
}

/////////////////////// transState servicer

void enter_f(StateMachine* state_machine) {
    // data.setup() & exit_f() prepare initial lcdBlState state
    data.lcdBlState.service();
    // going to hold?
    if (data.transState.getCurrentId() != Data::TransState::enter)
        D(F("Transition to hold"));
        // choose_updown() preserved in data.lcdblStateCache
        lcdbl_helper_init(Data::LcdBlState::on);
}

void hold_f(StateMachine* state_machine) {
    data.lcdBlState.service();
    // going to exit?
    if (data.transState.getCurrentId() != Data::TransState::hold)
        D(F("Transition to exit"));
        // this cycle's lcdBlState
        if ((data.lcdblStateCache != Data::LcdBlState::down) ||
            (data.lcdblStateCache != Data::LcdBlState::equal))
            lcdbl_helper_init(Data::LcdBlState::off);
        else
            lcdbl_helper_init(data.lcdblStateCache); // down or equal
}

void exit_f(StateMachine* state_machine) {
    data.lcdBlState.service();
    // going to enter?
    if (data.transState.getCurrentId() != Data::TransState::exit) {
        // Go to snooze or back to now?
        if (data.dispState.getCurrentId() == Data::DispState::four) {
            // back to now
            data.dispCycles++;
            if (data.dispCycles < Data::MAX_DISPLAY_CYCLES) { // back to now
                D(F("Setting up for display cycle: ")); DL(data.dispCycles);
                // new choice for next cycle
                choose_updown();  // sets lcdBlState ID
                data.dispState.setCurrentId(Data::DispState::now);
            } else {
                 D(F("Setting up for snooze"));
                 // to snooze
                 data.dispCycles = 0;
                 data.dispState.setCurrentId(Data::DispState::snooze);
            }
        }
        D(F("Transition to enter"));
        data.transState.setCurrentId(Data::TransState::enter);
        // enter always only handles up or equal
        if ((data.lcdblStateCache != Data::LcdBlState::up) ||
            (data.lcdblStateCache != Data::LcdBlState::equal))
            lcdbl_helper_init(Data::LcdBlState::off);
        else
            lcdbl_helper_init(data.lcdblStateCache); // up or equal
    }
}

//////////////////////// lcdBLState servicers

void lcdbl_state_helper(uint16_t lcdblTicks_end,
                  uint8_t lcdBlVal_end) {
    if (data.lcdblTicks < lcdblTicks_end) {
        if (data.lcdBlStateTimer.update())  // one tick passed
            data.lcdblTicks++;
        D(data.lcdblTicks); D(F("/")); DL(data.LCD_BL_RAMP_TICKS);
    } else { // done with this trans state
            data.lcdblTicks = 0;
            data.lcdBlVal = lcdBlVal_end;  // guarantee ending value
            data.transState.next();  // wraps to beginning if end
    }
    analogWrite(data.PIN_LCD_BL, data.lcdBlVal);
}

void lcdbl_state_up_f(StateMachine* state_machine) {
    if (data.transState.getCurrentId() == Data::TransState::enter) {
        D(F("Backlight up ramp "));
        lcdbl_state_helper(data.LCD_BL_RAMP_TICKS, 255);
    } else {
        // only enter handles up ramp
        data.transState.next();
    }
}

void lcdbl_state_equal_f(StateMachine* state_machine) {
    if ((data.transState.getCurrentId() == Data::TransState::enter) ||
        (data.transState.getCurrentId() == Data::TransState::exit)) {
        D(F("Backlight equal hold "));
        lcdbl_state_helper(data.LCD_BL_EQ_TICKS, 255);
    } else {
        // only enter/exit handles equal delay
        data.transState.next();
    }
}

void lcdbl_state_on_f(StateMachine* state_machine) {
    if (data.transState.getCurrentId() == Data::TransState::hold) {
        D(F("Backlight hold on "));
        lcdbl_state_helper(data.LCD_BL_ON_TICKS, 255);
    } else {
        // only hold does on
        data.transState.next();
    }
}

void lcdbl_state_down_f(StateMachine* state_machine) {
    if (data.transState.getCurrentId() == Data::TransState::exit) {
        D(F("Backlight down ramp "));
        lcdbl_state_helper(data.LCD_BL_RAMP_TICKS, 0);
    } else {
        // only exit does down ramp
        data.transState.next();
    }
}

void lcdbl_state_off_f(StateMachine* state_machine) {
    D(F("Backlight hold off "));
    lcdbl_state_helper(data.LCD_BL_OFF_TICKS, 0);
    // to be safe, always go back to enter
    data.transState.setCurrentId(Data::TransState::enter);
}

//////////////////////// lcdBlStateTimer servicers

void lcdbl_event_up_f(const TimedEvent* timed_event) {
    // prevent overflow
    if (data.lcdBlVal < 239)
        data.lcdBlVal += 16;
    else
        data.lcdBlVal = 255;
}

void lcdbl_event_down_f(const TimedEvent* timed_event) {
    // prevent underflow
    if (data.lcdBlVal > 17)
        data.lcdBlVal -= 16;
    else
        data.lcdBlVal = 0;
}

void lcdbl_event_equal_f(const TimedEvent* timed_event) {
    data.lcdBlVal = 255; // signal not done
}

void lcdbl_event_on_f(const TimedEvent* timed_event) {
    data.lcdBlVal = 255; // signal not done
}

void lcdbl_event_off_f(const TimedEvent* timed_event) {
    data.lcdBlVal = 0; // signal not done
}

//////////////////////// WTD sleep wakeup ISR
ISR(WDT_vect)
{
    data.sleepCycleCounter++;
}

void setup(void) {
    DL(F("Setting up..."));
    data.setup();
}

void loop(void) {
    DL(F("Looping..."));
    data.loop();
}
